# Fritzing sketch TTS (saved by Fritzing 0.9.3b)
breadboards: 1

parts:
  1Sheeld1 = 1Sheeld
  Part1 = Arduino Uno (Rev3) - ICSP  # not connected
  Part2 = RFID-RC522 [part_number=101218]
  DHT1 = DHT22 Humidity and Temperature Sensor
  DHT2 = DHT11 Humitidy and Temperature Sensor
  J1 = Piezo Speaker
  S1 = Momentary Switch [package=ksa_sealed_tac_switch]
  S2 = Momentary Switch [package=ksa_sealed_tac_switch]
  LCD1 = LCD screen
  LCM1602_IIC1 = LCM1602 IIC [part_number="LCM1602 IIC" chip_label="LCM1602 IIC" package="DIP (Dual Inline) [THT]"]

nets:
  N1: 1Sheeld1.D2, J1.pin2
  N2: 1Sheeld1.D3, DHT1.DATA
  N3: 1Sheeld1.D4, DHT2.DATA
  N4: 1Sheeld1.D9, Part2.RST
  N5: 1Sheeld1.D10, Part2.SDA
  N6: 1Sheeld1.D11, Part2.MOSI
  N7: 1Sheeld1.D12, Part2.MISO
  N8: 1Sheeld1.D13, Part2.SCK
  N9: 1Sheeld1.SDA, LCM1602_IIC1.SDA
  N10: 1Sheeld1.SCL, LCM1602_IIC1.SCL
  N11: 1Sheeld1.A0, S1.1
  N12: 1Sheeld1.A1, S2.1
  GND: 1Sheeld1.GND, Part2.GND, DHT1.GND, DHT2.GND, J1.pin1, S1.3, S2.3, LCM1602_IIC1.GND
  VDD: 1Sheeld1.5V, DHT1.VDD, DHT2.VDD, LCM1602_IIC1.VCC
  3.3V: 1Sheeld1.3.3V, Part2.3.3V
  VSS: LCD1.VSS, LCM1602_IIC1.VSS
  VDD_2: LCD1.VDD, LCM1602_IIC1.VDD
  N13: LCD1.V0, LCM1602_IIC1.V0
  N14: LCD1.RS, LCM1602_IIC1.RS
  N15: LCD1.R/W, LCM1602_IIC1.RW
  N16: LCD1.E, LCM1602_IIC1.E
  N17: LCD1.DB0, LCM1602_IIC1.D0
  N18: LCD1.DB1, LCM1602_IIC1.D1
  N19: LCD1.DB2, LCM1602_IIC1.D2
  N20: LCD1.DB3, LCM1602_IIC1.D3
  N21: LCD1.DB4, LCM1602_IIC1.D4
  N22: LCD1.DB5, LCM1602_IIC1.D5
  N23: LCD1.DB6, LCM1602_IIC1.D6
  N24: LCD1.DB7, LCM1602_IIC1.D7
  N25: LCD1.LED+, LCM1602_IIC1.A
  N26: LCD1.LED-, LCM1602_IIC1.K

notes:
  OUT DHT22
  IN DHT11
  LCD I2C

custom parts:
  1Sheeld: 1Sheeld is a new easily configured shield for Arduino. It is connected to a mobile app that allow the usage of all of Android smartphones' capabilities such as LCD Screen, Gyroscope, Switches, LEDs, Accelerometer, Magnetometer, GSM, Wi-Fi, GPS ...etc. into your Arduino sketch.
  DHT11 Humitidy and Temperature Sensor: DHT11 Humidity and Temperature Sensor
  LCM1602 IIC: I2C-Module to use a 1602 or 2004 LCD on with the wire.h libory Serial LCD Modul
