# Fritzing sketch servo_KM (saved by Fritzing 0.9.3b)
breadboards: 1

parts:
  Part1 = Arduino Uno (Rev3)
  U1 = LCD-16X2 [package=lcd-16x2]
  R1 = Trimmer Potentiometer [maximum_resistance=10kΩ package=THT]
  R2 = Trimmer Potentiometer [maximum_resistance=10kΩ package=THT]
  J1 = Basic Servo

nets:
  N1: Part1.A0, R2.wiper
  N2: Part1.D9_PWM, J1.pulse
  N3: Part1.D2, U1.DB7
  N4: Part1.D3_PWM, U1.DB6
  N5: Part1.D4, U1.DB5
  N6: Part1.D5_PWM, U1.DB4
  N7: Part1.D6_PWM, U1.E
  N8: Part1.D7, U1.RS
  5V: Part1.5V, U1.VDD, U1.A, R1.leg1, R2.leg2, J1.vcc
  GND: Part1.GND, U1.VSS, U1.R_W, U1.K, R1.leg2, R2.leg1, J1.gnd
  N9: U1.VO, R1.wiper
