# Fritzing sketch stoper_KM (saved by Fritzing 0.9.3b)
breadboards: 1

parts:
  Part1 = Arduino Uno (Rev3)
  S1 = Pushbutton [package="[THT]"]
  S2 = Pushbutton [package="[THT]"]
  U1 = LCD-16X2 [package=lcd-16x2]
  R1 = Trimmer Potentiometer [maximum_resistance=10kΩ package=THT]
  LED1 = LED - 5mm [color="Red (633nm)" package="5 mm [THT]"]
  LED2 = LED - 5mm [color="Red (633nm)" package="5 mm [THT]"]
  LED3 = LED - 5mm [color="Red (633nm)" package="5 mm [THT]"]
  LED4 = LED - 5mm [color="Green (555nm)" package="5 mm [THT]"]
  R2 = Resistor [tolerance=±5% resistance=220 package=THT]
  R3 = Resistor [tolerance=±5% resistance=220 package=THT]
  R4 = Resistor [tolerance=±5% resistance=220 package=THT]
  R5 = Resistor [tolerance=±5% resistance=220 package=THT]

nets:
  N1: Part1.A0, LED4.anode
  N2: Part1.A1, LED3.anode
  N3: Part1.A2, LED2.anode
  N4: Part1.A3, LED1.anode
  N5: Part1.D12/MISO, S2.Pin_1, S2.Pin_2
  N6: Part1.D13/SCK, S1.Pin_1, S1.Pin_2
  N7: Part1.D2, U1.DB7
  N8: Part1.D3_PWM, U1.DB6
  N9: Part1.D4, U1.DB5
  N10: Part1.D5_PWM, U1.DB4
  N11: Part1.D6_PWM, U1.E
  N12: Part1.D7, U1.RS
  5V: Part1.5V, U1.VDD, U1.A, R1.leg1
  GND: Part1.GND, S1.Pin_3, S1.Pin_4, S2.Pin_3, S2.Pin_4, U1.VSS, U1.R_W, U1.K, R1.leg2, R2.Pin_1, R3.Pin_1, R4.Pin_1, R5.Pin_1
  N13: U1.VO, R1.wiper
  N14: LED1.cathode, R5.Pin_0
  N15: LED2.cathode, R4.Pin_0
  N16: LED3.cathode, R3.Pin_0
  N17: LED4.cathode, R2.Pin_0
